# Fritzing sketch Pinout and Schematics (saved by Fritzing 0.9.3b)

parts:
  J1 = STM32 Nucleo boards [part_number=G474RE]
  Composant1 = MicroSD Card Module
  HC-SR04_Sensor_1 = HC-SR04 Ultrasonic Distance Sensor
  Composant2 = InvenSense MPU6050
  Composant3 = Adafruit_BMP280  # not connected
  QMC5883L = Boladge HMC5883L Compass Module
  Composant4 = Adafruit VL53L0X Time of Flight Distance Sensor [part_number="Adafruit #3317"]  # not connected
  HC-SR04_Sensor_2 = HC-SR04 Ultrasonic Distance Sensor
  HC-SR04_Sensor_3 = HC-SR04 Ultrasonic Distance Sensor [part_number="Sensor 3"]
  U1 = ESP32-38PinWide [part_number=ESP32-38PinWide]
  J2 = Piezo Speaker

nets:
  N1: J1.PC8, Composant2.SCL
  N2: J1.PC6, QMC5883L.SCL
  N3: J1.PB15, Composant1.MOSI
  N4: J1.PB14, Composant1.MISO
  N5: J1.PB13, Composant1.SCK
  N6: J1.PA6, HC-SR04_Sensor_3.ECHO
  N7: J1.PC7, QMC5883L.SDA
  N8: J1.PB10, HC-SR04_Sensor_1.TRIG
  N9: J1.PB5, Composant2.SDA
  N10: J1.PA0, HC-SR04_Sensor_1.ECHO
  N11: J1.PA4, Composant1.CS
  N12: J1.PB0, HC-SR04_Sensor_3.TRIG
  N13: J1.PC0, HC-SR04_Sensor_2.ECHO
  N14: J1.PC2, HC-SR04_Sensor_2.TRIG
  N15: U1.GND, J2.pin1
  N16: U1.GPIO23, J2.pin2

notes:
  +5v

custom parts:
  Adafruit_BMP280: Bosch has stepped up their game with their new BMP280 sensor, an environmental sensor with temperature, barometric pressure that is the next generation upgrade to the BMP085/BMP180/BMP183. This sensor is great for all sorts of weather sensing and can even be used in both I2C and SPI! This precision sensor from Bosch is the best low-cost, precision sensing solution for measuring barometric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
  Boladge HMC5883L Compass Module: Cheap digital compass module
  Adafruit VL53L0X Time of Flight Distance Sensor: The VL53L0X is a Time of Flight distance sensor like no other you've used! The sensor contains a very tiny invisible laser source, and a matching sensor. The VL53L0X can detect the "time of flight", or how long the light has taken to bounce back to the sensor. Since it uses a very narrow light source, it is good for determining distance of only the surface directly in front of it. Unlike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
  ESP32-38PinWide: Generic 38-Pin ESP32 with wide format (only access to one side of pins on a breadboard) based on Stephen Lilley's HiLetgo ESP-WROOM-32 ESP32 ESP-32S Development Board.
